# Fritzing sketch Placa (saved by Fritzing 0.9.3b)
breadboards: 1

parts:
  Gizwits_WiFi_Witty_ESP-12F1 = Gizwits WiFi Witty ESP-12F
  R1 = TRIMPOT [package=3362u-2]
  D1 = Diode [package=diode-1n4001]
  R2 = Photocell (LDR) [package=THT]
  DS1 = DS18B20 1-Wire Temperature Sensor [part_number=DS18B20]
  R3 = Resistor [tolerance=±5% resistance=220 package="2512 [SMD]"]
  R4 = Resistor [tolerance=±5% resistance=220 package="2512 [SMD]"]
  LED1 = LED - 5mm [color="Red (633nm)" package="5 mm [THT]"]
  LED2 = LED - 5mm [color="Green (570nm)" package="5 mm [THT]"]
  Componente1 = Soil Moisture Sensor
  J1 = screw terminal, 3 pins
  R5 = TRIMPOT [package=3362u-2]
  R6 = Resistor [tolerance=±5% resistance=220 package="2512 [SMD]"]
  D3 = Diode [package=diode-1n4001]

nets:
  N1: Gizwits_WiFi_Witty_ESP-12F1.ADC, D1.C, D3.C
  N2: Gizwits_WiFi_Witty_ESP-12F1.GPIO13, Componente1.VCC, J1.pin1
  VCC: Gizwits_WiFi_Witty_ESP-12F1.VCC, DS1.VDD, R4.Pin_0
  GND: Gizwits_WiFi_Witty_ESP-12F1.GND, R1.CCW, DS1.GND, R3.Pin_0, LED1.anode, LED2.anode, Componente1.GND, J1.pin3, R5.CW, R6.Pin_0
  N3: Gizwits_WiFi_Witty_ESP-12F1.GPIO15, R1.CW
  N4: Gizwits_WiFi_Witty_ESP-12F1.GPIO2, DS1.DQ, R4.Pin_1
  N5: Gizwits_WiFi_Witty_ESP-12F1.GPIO0, LED1.cathode
  N6: Gizwits_WiFi_Witty_ESP-12F1.GPIO5, LED2.cathode
  N7: R1.WIPER, R2.pin_0
  N8: R2.pin_1, R3.Pin_1
  N9: Componente1.SIG, R5.CCW
  N10: R5.WIPER, R6.Pin_1
